# Fritzing sketch 01-led (saved by Fritzing 1.0.5)
breadboards: 1

parts:
  Pico_H1 = Raspberry Pi Pico H
  R1 = Resistor [tolerance=±5% power=0.25W resistance=220 package=THT]
  LED1 = LED - 3mm [color="Red (633nm)" current=30mA package="3 mm [THT]"]

nets:
  N1: Pico_H1.GND, R1.Pin_1
  N2: Pico_H1.GP14, LED1.anode
  N3: R1.Pin_0, LED1.cathode

custom parts:
  Raspberry Pi Pico H: Raspberry Pi Pico H. Based around the RP2040 microcontroller the Pico H is a low cost microcontroller device bringing Raspberry Pi quality, cost, and easy of use to the microcontroller space.
