# Fritzing sketch 17-button (saved by Fritzing 1.0.5)
breadboards: 1

parts:
  A1 = Raspberry Pi Pico2
  S1 = Pushbutton [package="[THT]"]
  LED1 = smd LED [color="Red (633nm)" package="0603 [SMD]"]
  R1 = Resistor [tolerance=±5% power=0.25W resistance=220 package=THT]

nets:
  N1: A1.pin_3, A1.pin_8, A1.pin_13, A1.pin_18, A1.pin_23, A1.pin_28, A1.pin_33, A1.pin_38, S1.Pin_3, S1.Pin_4
  N2: A1.pin_17, S1.Pin_1, S1.Pin_2
  N3: A1.pin_19, LED1.anode
  N4: LED1.cathode, R1.Pin_0

custom parts:
  Raspberry Pi Pico2: Raspberry Pi Pico 2W is our new $7 microcontroller board, built on RP2350: our new high-performance, secure microcontroller with on board WiFi.
