# Fritzing sketch 21-temp-toggle-button (saved by Fritzing 1.0.5)
breadboards: 1

parts:
  A1 = Raspberry Pi Pico2
  DHT1 = Humidity and Temperature Sensor DHT11
  S1 = Pushbutton [package="[THT]"]

nets:
  N1: A1.pin_13, A1.pin_18, A1.pin_23, A1.pin_28, A1.pin_33, A1.pin_38, DHT1.GND_2
  N2: A1.pin_21, DHT1.Data-signal
  N3: DHT1.Vcc, S1.Pin_3, S1.Pin_4
  N4: S1.Pin_1, S1.Pin_2

custom parts:
  Raspberry Pi Pico2: Raspberry Pi Pico 2W is our new $7 microcontroller board, built on RP2350: our new high-performance, secure microcontroller with on board WiFi.
  Humidity and Temperature Sensor DHT11: Digital relative humidity & temperature sensor DHT11
