# Fritzing sketch 23-lcd-temp (saved by Fritzing 1.0.5)
breadboards: 1

parts:
  A1 = Raspberry Pi Pico2  # not connected
  DHT1 = Humidity and Temperature Sensor DHT11
  LCD1 = LCD screen  # not connected
  S1 = Pushbutton [package="[THT]"]

nets:
  N1: DHT1.GND_2, S1.Pin_3, S1.Pin_4
  N2: S1.Pin_1, S1.Pin_2

custom parts:
  Raspberry Pi Pico2: Raspberry Pi Pico 2W is our new $7 microcontroller board, built on RP2350: our new high-performance, secure microcontroller with on board WiFi.
  Humidity and Temperature Sensor DHT11: Digital relative humidity & temperature sensor DHT11
